# Fritzing sketch kettle (saved by Fritzing 1.0.4)
circuit board: 2cm x 11cm
breadboards: 2

parts:
  100K = Rotary Potentiometer (Small) [maximum_resistance=0.1MΩ knob_status=50% power=0.5W package=THT]
  100K_2 = Rotary Potentiometer (Small) [maximum_resistance=0.1MΩ knob_status=50% power=0.5W package=THT]
  IN1 = PJ-301M [part_number=PJ-301M]
  104 = Ceramic Capacitor [capacitance=100nF voltage=16V package="200 mil [THT, multilayer]"]
  IN2 = PJ-301M [part_number=PJ-301M]
  Out1 = PJ-301M [part_number=PJ-301M]
  IN3 = PJ-301M [part_number=PJ-301M]
  IN4 = PJ-301M [part_number=PJ-301M]
  100k = Rotary Potentiometer (Small) [maximum_resistance=0.1MΩ knob_status=50% power=0.5W package=THT]
  100k_2 = Rotary Potentiometer (Small) [maximum_resistance=0.1MΩ knob_status=50% power=0.5W package=THT]
  Out2 = PJ-301M [part_number=PJ-301M]
  J3 = shrouded pin header, 10 pins [form="♂ (shrouded male)"]
  100uF = Electrolytic Capacitor [capacitance=0.1mF voltage=35V package="100 mil [THT, electrolytic]"]
  4001 = Diode [package=diode-1n4148]
  J5 = female pin header, 1 pin [form="♀ (female)"]
  2N3904 = NPN-Transistor [package="TO92 [THT]"]
  10K = Resistor [tolerance=±5% power=0.25W resistance=10k package=THT]
  2N3904_2 = NPN-Transistor [package="TO92 [THT]"]
  10K_2 = Resistor [tolerance=±5% power=0.25W resistance=10k package=THT]
  104_2 = Ceramic Capacitor [capacitance=100nF voltage=16V package="200 mil [THT, multilayer]"]
  104_3 = Ceramic Capacitor [capacitance=100nF voltage=16V package="200 mil [THT, multilayer]"]
  1K = Resistor [tolerance=±1% power=0.25W resistance=1k package=THT]
  1K1 = Resistor [tolerance=±1% power=0.25W resistance=1k package=THT]
  2N3904_3 = NPN-Transistor [package="TO92 [THT]"]
  104_4 = Ceramic Capacitor [capacitance=100nF voltage=16V package="200 mil [THT, multilayer]"]
  10K_3 = Resistor [tolerance=±5% power=0.25W resistance=10k package=THT]
  2N3904_4 = NPN-Transistor [package="TO92 [THT]"]
  104_5 = Ceramic Capacitor [capacitance=100nF voltage=16V package="200 mil [THT, multilayer]"]
  10K_4 = Resistor [tolerance=±5% power=0.25W resistance=10k package=THT]
  1K_2 = Resistor [tolerance=±1% power=0.25W resistance=1k package=THT]
  1K_3 = Resistor [tolerance=±1% power=0.25W resistance=1k package=THT]

nets:
  N1: 100K.leg1, 100K.wiper, 2N3904_4.C, 1K_3.Pin_0
  N2: 100K.leg2, 2N3904_4.E, 104_5.0, 10K_4.Pin_1
  N3: 100K_2.leg1, 100K_2.wiper, 2N3904_3.C, 1K_2.Pin_0
  N4: 100K_2.leg2, 2N3904_3.E, 104_4.1, 10K_3.Pin_1
  GND: IN1.Pin_1, 104.1, IN2.Pin_1, Out1.Pin_1, IN3.Pin_1, IN4.Pin_1, Out2.Pin_1, J3.pin2, J3.pin3, J3.pin4, J3.pin7, J3.pin8, J3.pin9, 100uF.-, 2N3904.B, 2N3904_2.B, 2N3904_3.B, 2N3904_4.B
  N5: IN1.Pin_3, 1K_2.Pin_1
  N6: 104.0, 100uF.+, 4001.C, J5.pin1, 10K.Pin_0, 10K_2.Pin_0, 10K_3.Pin_0, 10K_4.Pin_0
  N7: IN2.Pin_3, 1K_3.Pin_1
  N8: Out1.Pin_3, 104_4.0, 104_5.1
  N9: IN3.Pin_3, 1K1.Pin_1
  N10: IN4.Pin_3, 1K.Pin_1
  N11: 100k.leg1, 100k.wiper, 2N3904_2.C, 1K1.Pin_0
  N12: 100k.leg2, 2N3904_2.E, 10K_2.Pin_1, 104_2.1
  N13: 100k_2.leg1, 100k_2.wiper, 2N3904.C, 1K.Pin_0
  N14: 100k_2.leg2, 2N3904.E, 10K.Pin_1, 104_3.0
  N15: Out2.Pin_3, 104_2.0, 104_3.1
  N16: J3.pin1, J3.pin10
  N17: J3.pin5, J3.pin6, 4001.A

notes:
  kettle
  blueprint@poetaster . de
  jlcjlcjlcjlcjlc

custom parts:
  PJ-301M: Phone power jack.
